// Digital circuit ADD 1 Bit.dig as structural Verilog
module ADD_1_Bit (
  input  A,
  input  B,
  input  Cin,
  output S,
  output Cout
);

  wire and_1_out, and_2_out, xor_1_out, xor_2_out;

  xor xor_1 (xor_1_out, Cin, B);
  and and_1 (and_1_out, B, A);
  xor xor_2 (xor_2_out, B, A);
  xor xor_3 (S, xor_1_out, A);
  and and_2 (and_2_out, Cin, xor_2_out);
  or or_1 (Cout, and_1_out, and_2_out);
endmodule
