// Digital circuit ADD 8 Bit.dig as structural Verilog
module ADD_8_Bit (
  input  A7,
  input  A6,
  input  A5,
  input  A4,
  input  A3,
  input  A2,
  input  A1,
  input  A0,
  input  B7,
  input  B6,
  input  B5,
  input  B4,
  input  B2,
  input  B1,
  input  B3,
  input  B0,
  input  Cin,
  output Cout,
  output S0,
  output S1,
  output S2,
  output S3,
  output S4,
  output S5,
  output S6,
  output S7
);

  wire add_1_bit_1_cout, add_1_bit_2_cout, add_1_bit_3_cout, add_1_bit_4_cout, add_1_bit_5_cout,
       add_1_bit_6_cout, add_1_bit_7_cout;

  ADD_1_Bit add_1_bit_1 (.A(A0), .B(B0), .Cin(Cin), .S(S0), .Cout(add_1_bit_1_cout));
  ADD_1_Bit add_1_bit_2 (.A(A1), .B(B1), .Cin(add_1_bit_1_cout), .S(S1), .Cout(add_1_bit_2_cout));
  ADD_1_Bit add_1_bit_3 (.A(A2), .B(B2), .Cin(add_1_bit_2_cout), .S(S2), .Cout(add_1_bit_3_cout));
  ADD_1_Bit add_1_bit_4 (.A(A3), .B(B3), .Cin(add_1_bit_3_cout), .S(S3), .Cout(add_1_bit_4_cout));
  ADD_1_Bit add_1_bit_5 (.A(A4), .B(B4), .Cin(add_1_bit_4_cout), .S(S4), .Cout(add_1_bit_5_cout));
  ADD_1_Bit add_1_bit_6 (.A(A5), .B(B5), .Cin(add_1_bit_5_cout), .S(S5), .Cout(add_1_bit_6_cout));
  ADD_1_Bit add_1_bit_7 (.A(A6), .B(B6), .Cin(add_1_bit_6_cout), .S(S6), .Cout(add_1_bit_7_cout));
  ADD_1_Bit add_1_bit_8 (.A(A7), .B(B7), .Cin(add_1_bit_7_cout), .S(S7), .Cout(Cout));
endmodule
