// Digital circuit MUX 2-1.dig as structural Verilog
module MUX_2_1 (
  input  A,
  input  B,
  input  C,
  output S
);

  wire and_1_out, and_2_out, not_1_out;

  not not_1 (not_1_out, C);
  and and_1 (and_1_out, not_1_out, A);
  and and_2 (and_2_out, C, B);
  or or_1 (S, and_1_out, and_2_out);
endmodule
