// Digital circuit MUX 8-recursif.dig as structural Verilog
module MUX_8_recursif (
  input  E0,
  input  E1,
  input  E2,
  input  E3,
  input  E4,
  input  E5,
  input  E6,
  input  E7,
  input  C0,
  input  C2,
  input  C1,
  output out_12
);

  wire mux_2_1_1_s, mux_2_1_2_s, mux_2_1_3_s, mux_2_1_4_s, mux_2_1_5_s, mux_2_1_6_s;

  MUX_2_1 mux_2_1_1 (.A(E0), .B(E1), .C(C0), .S(mux_2_1_1_s));
  MUX_2_1 mux_2_1_2 (.A(E2), .B(E3), .C(C0), .S(mux_2_1_2_s));
  MUX_2_1 mux_2_1_3 (.A(E4), .B(E5), .C(C0), .S(mux_2_1_3_s));
  MUX_2_1 mux_2_1_4 (.A(E6), .B(E7), .C(C0), .S(mux_2_1_4_s));
  MUX_2_1 mux_2_1_5 (.A(mux_2_1_1_s), .B(mux_2_1_2_s), .C(C1), .S(mux_2_1_5_s));
  MUX_2_1 mux_2_1_6 (.A(mux_2_1_3_s), .B(mux_2_1_4_s), .C(C1), .S(mux_2_1_6_s));
  MUX_2_1 mux_2_1_7 (.A(mux_2_1_5_s), .B(mux_2_1_6_s), .C(C2), .S(out_12));
endmodule
