// Digital circuit decodeur 3-8.dig as structural Verilog
module decodeur_3_8 (
  input  in_1,
  input  in_2,
  input  in_3,
  output out_4,
  output out_5,
  output out_6,
  output out_7,
  output out_8,
  output out_9,
  output out_10,
  output out_11
);

  wire and_1_out, and_2_out, and_3_out, and_4_out, and_5_out, and_6_out, and_7_out, and_8_out, not_1_out,
       not_2_out, not_3_out, not_4_out, not_5_out, not_6_out, not_7_out, not_8_out, not_9_out, not_10_out,
       not_11_out, not_12_out;

  and and_1 (and_1_out, not_1_out, not_2_out);
  not not_1 (not_1_out, in_1);
  not not_2 (not_2_out, in_2);
  and and_2 (and_2_out, not_3_out, not_4_out);
  not not_3 (not_3_out, in_1);
  not not_4 (not_4_out, in_2);
  and and_3 (and_3_out, not_5_out, in_2);
  not not_5 (not_5_out, in_1);
  and and_4 (and_4_out, not_6_out, in_2);
  not not_6 (not_6_out, in_1);
  and and_5 (and_5_out, in_1, not_7_out);
  not not_7 (not_7_out, in_2);
  and and_6 (and_6_out, in_1, not_8_out);
  not not_8 (not_8_out, in_2);
  and and_7 (and_7_out, in_1, in_2);
  and and_8 (and_8_out, in_1, in_2);
  not not_9 (not_9_out, in_3);
  and and_9 (out_4, and_1_out, not_10_out);
  not not_10 (not_10_out, in_3);
  and and_10 (out_5, and_2_out, in_3);
  and and_11 (out_6, and_3_out, not_9_out);
  and and_12 (out_7, and_4_out, in_3);
  and and_13 (out_8, and_5_out, not_11_out);
  not not_11 (not_11_out, in_3);
  and and_14 (out_9, and_6_out, in_3);
  and and_15 (out_10, and_7_out, not_12_out);
  not not_12 (not_12_out, in_3);
  and and_16 (out_11, and_8_out, in_3);
endmodule
