// Digital circuit BasculeD 8bits.dig as structural Verilog
module BasculeD_8bits (
  input  in_1,
  input  in_2,
  output out_3,
  output out_4,
  output out_5,
  output out_6,
  output out_7,
  output out_8,
  output out_9,
  output out_10,
  output out_11,
  output out_12,
  output out_13,
  output out_14,
  output out_15,
  output out_16,
  output out_17,
  output out_18
);

  D_FF d_ff_1 (.D(in_1), .C(in_2), .Q(out_3), .nQ(out_4));
  D_FF d_ff_2 (.D(in_1), .C(in_2), .Q(out_5), .nQ(out_6));
  D_FF d_ff_3 (.D(in_1), .C(in_2), .Q(out_7), .nQ(out_8));
  D_FF d_ff_4 (.D(in_1), .C(in_2), .Q(out_9), .nQ(out_10));
  D_FF d_ff_5 (.D(in_1), .C(in_2), .Q(out_11), .nQ(out_12));
  D_FF d_ff_6 (.D(in_1), .C(in_2), .Q(out_13), .nQ(out_14));
  D_FF d_ff_7 (.D(in_1), .C(in_2), .Q(out_15), .nQ(out_16));
  D_FF d_ff_8 (.D(in_1), .C(in_2), .Q(out_17), .nQ(out_18));
endmodule
