// Digital circuit Banc registre 32 bits.dig as structural Verilog
module Banc_registre_32_bits (
  input  [4:0] Rd,
  input  W_reg,
  input  [31:0] Res,
  input  [4:0] Rs1,
  input  [4:0] Rs2,
  output [31:0] Src1,
  output [31:0] Src2
);

  wire and_1_out, and_2_out, and_3_out, and_4_out, decoder_1_out_0, decoder_1_out_1, decoder_1_out_2,
       decoder_1_out_3;
  wire [31:0] banc_registre_8_bits_1_rs1, banc_registre_8_bits_1_rs2, banc_registre_8_bits_sans_0_1_rs1,
       banc_registre_8_bits_sans_0_1_rs2, banc_registre_8_bits_sans_0_2_rs1,
       banc_registre_8_bits_sans_0_2_rs2, banc_registre_8_bits_sans_0_3_rs1,
       banc_registre_8_bits_sans_0_3_rs2;

  Decoder #(.Selector_Bits(2)) decoder_1 (
    .sel(Rd[4:3]), .out_0(decoder_1_out_0), .out_1(decoder_1_out_1), .out_2(decoder_1_out_2),
    .out_3(decoder_1_out_3));
  and and_1 (and_1_out, decoder_1_out_0, W_reg);
  and and_2 (and_2_out, decoder_1_out_1, W_reg);
  and and_3 (and_3_out, decoder_1_out_2, W_reg);
  and and_4 (and_4_out, decoder_1_out_3, W_reg);
  Banc_Registre_8_bits banc_registre_8_bits_1 (
    .Rd(Rd[2:0]), .W_reg(and_1_out), .Res(Res), .R1(Rs1[2:0]), .R2(Rs2[2:0]),
    .Rs1(banc_registre_8_bits_1_rs1), .Rs2(banc_registre_8_bits_1_rs2));
  Banc_registre_8_bits_sans_0 banc_registre_8_bits_sans_0_1 (
    .Rd(Rd[2:0]), .W_reg(and_2_out), .Res(Res), .R1(Rs1[2:0]), .R2(Rs2[2:0]),
    .Rs1(banc_registre_8_bits_sans_0_1_rs1), .Rs2(banc_registre_8_bits_sans_0_1_rs2));
  Banc_registre_8_bits_sans_0 banc_registre_8_bits_sans_0_2 (
    .Rd(Rd[2:0]), .W_reg(and_3_out), .Res(Res), .R1(Rs1[2:0]), .R2(Rs2[2:0]),
    .Rs1(banc_registre_8_bits_sans_0_2_rs1), .Rs2(banc_registre_8_bits_sans_0_2_rs2));
  Banc_registre_8_bits_sans_0 banc_registre_8_bits_sans_0_3 (
    .Rd(Rd[2:0]), .W_reg(and_4_out), .Res(Res), .R1(Rs1[2:0]), .R2(Rs2[2:0]),
    .Rs1(banc_registre_8_bits_sans_0_3_rs1), .Rs2(banc_registre_8_bits_sans_0_3_rs2));
  Multiplexer #(.Selector_Bits(2), .Bits(32)) multiplexer_1 (
    .sel(Rs1[4:3]), .in_0(banc_registre_8_bits_1_rs1), .in_1(banc_registre_8_bits_sans_0_1_rs1),
    .in_2(banc_registre_8_bits_sans_0_2_rs1), .in_3(banc_registre_8_bits_sans_0_3_rs1), .out(Src1));
  Multiplexer #(.Selector_Bits(2), .Bits(32)) multiplexer_2 (
    .sel(Rs2[4:3]), .in_0(banc_registre_8_bits_1_rs2), .in_1(banc_registre_8_bits_sans_0_1_rs2),
    .in_2(banc_registre_8_bits_sans_0_2_rs2), .in_3(banc_registre_8_bits_sans_0_3_rs2), .out(Src2));
endmodule
