// Digital circuit Banc registre 8 bits sans 0.dig as structural Verilog
module Banc_registre_8_bits_sans_0 (
  input  [2:0] Rd,
  input  W_reg,
  input  [31:0] Res,
  input  [2:0] R1,
  input  [2:0] R2,
  output [31:0] Rs1,
  output [31:0] Rs2
);

  wire and_1_out, and_2_out, and_3_out, and_4_out, and_5_out, and_6_out, and_7_out, and_8_out,
       decoder_1_out_0, decoder_1_out_1, decoder_1_out_2, decoder_1_out_3, decoder_1_out_4, decoder_1_out_5,
       decoder_1_out_6, decoder_1_out_7, decoder_2_out_0, decoder_2_out_1, decoder_2_out_2, decoder_2_out_3,
       decoder_2_out_4, decoder_2_out_5, decoder_2_out_6, decoder_2_out_7, decoder_3_out_0, decoder_3_out_1,
       decoder_3_out_2, decoder_3_out_3, decoder_3_out_4, decoder_3_out_5, decoder_3_out_6, decoder_3_out_7;
  wire [31:0] d_ff_1_q, d_ff_2_q, d_ff_3_q, d_ff_4_q, d_ff_5_q, d_ff_6_q, d_ff_7_q, d_ff_8_q;

  Decoder #(.Selector_Bits(3)) decoder_1 (
    .sel(Rd), .out_0(decoder_1_out_0), .out_1(decoder_1_out_1), .out_2(decoder_1_out_2),
    .out_3(decoder_1_out_3), .out_4(decoder_1_out_4), .out_5(decoder_1_out_5), .out_6(decoder_1_out_6),
    .out_7(decoder_1_out_7));
  and and_1 (and_1_out, decoder_1_out_0, W_reg);
  and and_2 (and_2_out, decoder_1_out_1, W_reg);
  and and_3 (and_3_out, decoder_1_out_2, W_reg);
  and and_4 (and_4_out, decoder_1_out_3, W_reg);
  and and_5 (and_5_out, decoder_1_out_4, W_reg);
  and and_6 (and_6_out, decoder_1_out_5, W_reg);
  and and_7 (and_7_out, decoder_1_out_6, W_reg);
  and and_8 (and_8_out, decoder_1_out_7, W_reg);
  D_FF #(.Bits(32)) d_ff_1 (.D(Res), .C(and_1_out), .Q(d_ff_1_q));  // open: nQ
  D_FF #(.Bits(32)) d_ff_2 (.D(Res), .C(and_2_out), .Q(d_ff_2_q));  // open: nQ
  D_FF #(.Bits(32)) d_ff_3 (.D(Res), .C(and_3_out), .Q(d_ff_3_q));  // open: nQ
  D_FF #(.Bits(32)) d_ff_4 (.D(Res), .C(and_4_out), .Q(d_ff_4_q));  // open: nQ
  D_FF #(.Bits(32)) d_ff_5 (.D(Res), .C(and_5_out), .Q(d_ff_5_q));  // open: nQ
  D_FF #(.Bits(32)) d_ff_6 (.D(Res), .C(and_6_out), .Q(d_ff_6_q));  // open: nQ
  D_FF #(.Bits(32)) d_ff_7 (.D(Res), .C(and_7_out), .Q(d_ff_7_q));  // open: nQ
  D_FF #(.Bits(32)) d_ff_8 (.D(Res), .C(and_8_out), .Q(d_ff_8_q));  // open: nQ
  assign Rs1 = decoder_2_out_0 ? d_ff_1_q : 32'bz;  // Driver driver_1
  assign Rs1 = decoder_2_out_1 ? d_ff_2_q : 32'bz;  // Driver driver_2
  Decoder #(.Selector_Bits(3)) decoder_2 (
    .sel(R1), .out_0(decoder_2_out_0), .out_1(decoder_2_out_1), .out_2(decoder_2_out_2),
    .out_3(decoder_2_out_3), .out_4(decoder_2_out_4), .out_5(decoder_2_out_5), .out_6(decoder_2_out_6),
    .out_7(decoder_2_out_7));
  assign Rs1 = decoder_2_out_2 ? d_ff_3_q : 32'bz;  // Driver driver_3
  assign Rs1 = decoder_2_out_3 ? d_ff_4_q : 32'bz;  // Driver driver_4
  assign Rs1 = decoder_2_out_4 ? d_ff_5_q : 32'bz;  // Driver driver_5
  assign Rs1 = decoder_2_out_5 ? d_ff_6_q : 32'bz;  // Driver driver_6
  assign Rs1 = decoder_2_out_6 ? d_ff_7_q : 32'bz;  // Driver driver_7
  assign Rs1 = decoder_2_out_7 ? d_ff_8_q : 32'bz;  // Driver driver_8
  assign Rs2 = decoder_3_out_0 ? d_ff_1_q : 32'bz;  // Driver driver_9
  assign Rs2 = decoder_3_out_1 ? d_ff_2_q : 32'bz;  // Driver driver_10
  Decoder #(.Selector_Bits(3)) decoder_3 (
    .sel(R2), .out_0(decoder_3_out_0), .out_1(decoder_3_out_1), .out_2(decoder_3_out_2),
    .out_3(decoder_3_out_3), .out_4(decoder_3_out_4), .out_5(decoder_3_out_5), .out_6(decoder_3_out_6),
    .out_7(decoder_3_out_7));
  assign Rs2 = decoder_3_out_2 ? d_ff_3_q : 32'bz;  // Driver driver_11
  assign Rs2 = decoder_3_out_3 ? d_ff_4_q : 32'bz;  // Driver driver_12
  assign Rs2 = decoder_3_out_4 ? d_ff_5_q : 32'bz;  // Driver driver_13
  assign Rs2 = decoder_3_out_5 ? d_ff_6_q : 32'bz;  // Driver driver_14
  assign Rs2 = decoder_3_out_6 ? d_ff_7_q : 32'bz;  // Driver driver_15
  assign Rs2 = decoder_3_out_7 ? d_ff_8_q : 32'bz;  // Driver driver_16
endmodule
