// Digital circuit Datapath 1.1.dig as structural Verilog
module Datapath_1_1 (
  input  G_ALU,
  input  G_PC,
  input  W_PC,
  input  W_RI,
  input  W_REG,
  input  MUX_ALU,
  input  G_MDR,
  input  W_MAR,
  input  W_MDR
);

  wire [31:0] add_1_s, banc_registre_32_bits_1_src1, banc_registre_32_bits_1_src2, bitextender_1_out,
       driver_1_out, MAR_q, MDR_q, multiplexer_1_out, PC_q, RAM_d, RI_q, ual_sans_shift_1_s0;

  D_FF #(.Bits(32)) PC (.D(add_1_s), .C(W_PC), .Q(PC_q));  // open: nQ
  Add #(.Bits(32)) add_1 (.a(PC_q), .b(32'h4), .c_i(1'b0), .s(add_1_s));  // open: c_o
  assign driver_1_out = G_PC ? PC_q : 32'bz;  // Driver driver_1
  D_FF #(.Bits(32)) RI (.D(driver_1_out), .C(W_RI), .Q(RI_q));  // open: nQ
  D_FF #(.Bits(32)) MAR (.D(driver_1_out), .C(W_MAR), .Q(MAR_q));  // open: nQ
  RAMSinglePortSel #(.AddrBits(6), .Bits(32)) RAM (.A(MAR_q[7:2]), .CS(1'b1), .WE(1'b0), .OE(1'b1), .D(RAM_d));
  Banc_registre_32_bits banc_registre_32_bits_1 (
    .Rd(RI_q[11:7]), .W_reg(W_REG), .Res(driver_1_out), .Rs1(RI_q[19:15]), .Rs2(RI_q[24:20]),
    .Src1(banc_registre_32_bits_1_src1), .Src2(banc_registre_32_bits_1_src2));
  BitExtender #(.inputBits(12), .outputBits(32)) bitextender_1 (.in(RI_q[31:20]), .out(bitextender_1_out));
  Multiplexer #(.Bits(32)) multiplexer_1 (
    .sel(MUX_ALU), .in_0(banc_registre_32_bits_1_src2), .in_1(bitextender_1_out), .out(multiplexer_1_out));
  D_FF #(.Bits(32)) MDR (.D(RAM_d), .C(W_MDR), .Q(MDR_q));  // open: nQ
  assign driver_1_out = G_MDR ? MDR_q : 32'bz;  // Driver driver_2
  UAL_sans_shift ual_sans_shift_1 (
    .A(banc_registre_32_bits_1_src1), .B(multiplexer_1_out), .SUB(RI_q[30]), .fct3(RI_q[14:12]),
    .S0(ual_sans_shift_1_s0));
  assign driver_1_out = G_ALU ? ual_sans_shift_1_s0 : 32'bz;  // Driver driver_3
endmodule
