// Digital circuit UAL sans shift.dig as structural Verilog
module UAL_sans_shift (
  input  [31:0] A,
  input  [31:0] B,
  input  SUB,
  input  [2:0] fct3,
  output [31:0] S0
);

  wire [31:0] add_1_s, and_1_out, multiplexer_1_out, or_1_out, sub_1_s, xor_1_out;

  Add #(.Bits(32)) add_1 (.a(A), .b(B), .c_i(1'b0), .s(add_1_s));  // open: c_o
  Sub #(.Bits(32)) sub_1 (.a(A), .b(B), .c_i(1'b0), .s(sub_1_s));  // open: c_o
  assign xor_1_out = A ^ B;  // XOr xor_1, 32 bits wide
  assign or_1_out = A | B;  // Or or_1, 32 bits wide
  assign and_1_out = A & B;  // And and_1, 32 bits wide
  Multiplexer #(.Bits(32)) multiplexer_1 (.sel(SUB), .in_0(add_1_s), .in_1(sub_1_s), .out(multiplexer_1_out));
  Multiplexer #(.Selector_Bits(3), .Bits(32)) multiplexer_2 (
    .sel(fct3), .in_0(multiplexer_1_out), .in_1({32{1'b0}}), .in_2({32{1'b0}}), .in_3({32{1'b0}}),
    .in_4(xor_1_out), .in_5({32{1'b0}}), .in_6(or_1_out), .in_7(and_1_out), .out(S0));
endmodule
