// Digital circuit ADDGP_1_bit.dig as structural Verilog
module ADDGP_1_bit (
  input  E_1,
  input  E_2,
  input  C_In,
  output S,
  output G,
  output P
);

  wire xor_1_out;

  xor xor_1 (xor_1_out, E_1, E_2);
  or or_1 (P, E_1, E_2);
  and and_1 (G, E_1, E_2);
  xor xor_2 (S, C_In, xor_1_out);
endmodule
