// Digital circuit ADDGP_8_BITS.dig as structural Verilog
module ADDGP_8_BITS (
  input  A_0,
  input  B_0,
  input  A_1,
  input  B_1,
  input  A_2,
  input  B_2,
  input  A_3,
  input  B_3,
  input  A_4,
  input  B_4,
  input  A_5,
  input  B_5,
  input  A_6,
  input  B_6,
  input  A_7,
  input  B_7,
  input  C_in,
  output S_0,
  output S_1,
  output S_2,
  output S_3,
  output S_4,
  output S_5,
  output S_6,
  output S_7,
  output C_out
);

  wire addgp_1_bit_1_g, addgp_1_bit_1_p, addgp_1_bit_2_g, addgp_1_bit_2_p, addgp_1_bit_3_g, addgp_1_bit_3_p,
       addgp_1_bit_4_g, addgp_1_bit_4_p, addgp_1_bit_5_g, addgp_1_bit_5_p, addgp_1_bit_6_g, addgp_1_bit_6_p,
       addgp_1_bit_7_g, addgp_1_bit_7_p, addgp_1_bit_8_g, addgp_1_bit_8_p, cc_8bits_1_1_s_0,
       cc_8bits_1_1_s_1, cc_8bits_1_1_s_2, cc_8bits_1_1_s_3, cc_8bits_1_1_s_4, cc_8bits_1_1_s_5,
       cc_8bits_1_1_s_6, cc_8bits_1_1_s_7;

  ADDGP_1_bit addgp_1_bit_1 (
    .E_1(A_0), .E_2(B_0), .C_In(cc_8bits_1_1_s_0), .S(S_0), .G(addgp_1_bit_1_g), .P(addgp_1_bit_1_p));
  ADDGP_1_bit addgp_1_bit_2 (
    .E_1(A_1), .E_2(B_1), .C_In(cc_8bits_1_1_s_1), .S(S_1), .G(addgp_1_bit_2_g), .P(addgp_1_bit_2_p));
  ADDGP_1_bit addgp_1_bit_3 (
    .E_1(A_2), .E_2(B_2), .C_In(cc_8bits_1_1_s_2), .S(S_2), .G(addgp_1_bit_3_g), .P(addgp_1_bit_3_p));
  ADDGP_1_bit addgp_1_bit_4 (
    .E_1(A_3), .E_2(B_3), .C_In(cc_8bits_1_1_s_3), .S(S_3), .G(addgp_1_bit_4_g), .P(addgp_1_bit_4_p));
  ADDGP_1_bit addgp_1_bit_5 (
    .E_1(A_4), .E_2(B_4), .C_In(cc_8bits_1_1_s_4), .S(S_4), .G(addgp_1_bit_5_g), .P(addgp_1_bit_5_p));
  ADDGP_1_bit addgp_1_bit_6 (
    .E_1(A_5), .E_2(B_5), .C_In(cc_8bits_1_1_s_5), .S(S_5), .G(addgp_1_bit_6_g), .P(addgp_1_bit_6_p));
  ADDGP_1_bit addgp_1_bit_7 (
    .E_1(A_6), .E_2(B_6), .C_In(cc_8bits_1_1_s_6), .S(S_6), .G(addgp_1_bit_7_g), .P(addgp_1_bit_7_p));
  ADDGP_1_bit addgp_1_bit_8 (
    .E_1(A_7), .E_2(B_7), .C_In(cc_8bits_1_1_s_7), .S(S_7), .G(addgp_1_bit_8_g), .P(addgp_1_bit_8_p));
  CC_8bits_1 cc_8bits_1_1 (
    .P_0(addgp_1_bit_1_p), .P_1(addgp_1_bit_2_p), .P_2(addgp_1_bit_3_p), .P_3(addgp_1_bit_4_p),
    .P_4(addgp_1_bit_5_p), .P_5(addgp_1_bit_6_p), .G_0(addgp_1_bit_1_g), .G_1(addgp_1_bit_2_g),
    .G_2(addgp_1_bit_3_g), .G_3(addgp_1_bit_4_g), .G_4(addgp_1_bit_5_g), .G_5(addgp_1_bit_6_g),
    .G_6(addgp_1_bit_7_g), .P_6(addgp_1_bit_7_p), .C_0(C_in), .G_7(addgp_1_bit_8_g), .P_7(addgp_1_bit_8_p),
    .S_0(cc_8bits_1_1_s_0), .S_1(cc_8bits_1_1_s_1), .S_2(cc_8bits_1_1_s_2), .S_3(cc_8bits_1_1_s_3),
    .S_4(cc_8bits_1_1_s_4), .S_5(cc_8bits_1_1_s_5), .S_6(cc_8bits_1_1_s_6), .S_7(cc_8bits_1_1_s_7),
    .S_8(C_out));
endmodule
