// Digital circuit ADD_1_bit.dig as structural Verilog
module ADD_1_bit (
  input  E0,
  input  E1,
  input  C_In,
  output S,
  output C_Out
);

  wire and_1_out, and_2_out, xor_1_out;

  xor xor_1 (xor_1_out, E0, E1);
  and and_1 (and_1_out, E0, E1);
  and and_2 (and_2_out, C_In, xor_1_out);
  xor xor_2 (S, xor_1_out, C_In);
  or or_1 (C_Out, and_1_out, and_2_out);
endmodule
