// Digital circuit ADD_8_bit.dig as structural Verilog
module ADD_8_bit (
  input  A_0,
  input  A_1,
  input  A_2,
  input  A_3,
  input  A_4,
  input  A_5,
  input  A_6,
  input  A_7,
  input  B_0,
  input  B_1,
  input  B_2,
  input  B_3,
  input  B_4,
  input  B_5,
  input  B_6,
  input  B_7,
  input  C_In,
  output S_0,
  output S_1,
  output S_2,
  output S_3,
  output S_4,
  output S_5,
  output S_6,
  output S_7
);

  wire add_1_bit_1_c_out, add_1_bit_2_c_out, add_1_bit_3_c_out, add_1_bit_4_c_out, add_1_bit_5_c_out,
       add_1_bit_6_c_out, add_1_bit_7_c_out;

  ADD_1_bit add_1_bit_1 (.E0(A_0), .E1(B_0), .C_In(C_In), .S(S_0), .C_Out(add_1_bit_1_c_out));
  ADD_1_bit add_1_bit_2 (.E0(A_1), .E1(B_1), .C_In(add_1_bit_1_c_out), .S(S_1), .C_Out(add_1_bit_2_c_out));
  ADD_1_bit add_1_bit_3 (.E0(A_2), .E1(B_2), .C_In(add_1_bit_2_c_out), .S(S_2), .C_Out(add_1_bit_3_c_out));
  ADD_1_bit add_1_bit_4 (.E0(A_3), .E1(B_3), .C_In(add_1_bit_3_c_out), .S(S_3), .C_Out(add_1_bit_4_c_out));
  ADD_1_bit add_1_bit_5 (.E0(A_4), .E1(B_4), .C_In(add_1_bit_4_c_out), .S(S_4), .C_Out(add_1_bit_5_c_out));
  ADD_1_bit add_1_bit_6 (.E0(A_5), .E1(B_5), .C_In(add_1_bit_5_c_out), .S(S_5), .C_Out(add_1_bit_6_c_out));
  ADD_1_bit add_1_bit_7 (.E0(A_6), .E1(B_6), .C_In(add_1_bit_6_c_out), .S(S_6), .C_Out(add_1_bit_7_c_out));
  ADD_1_bit add_1_bit_8 (.E0(A_7), .E1(B_7), .C_In(add_1_bit_7_c_out), .C_Out(S_7));  // open: S
endmodule
