// Digital circuit Barrel_shifter.dig as structural Verilog
module Barrel_shifter (
  input  E_0,
  input  E_1,
  input  E_2,
  input  E_3,
  input  E_4,
  input  E_5,
  input  E_6,
  input  E_7,
  input  D_0,
  input  D_1,
  output S_0,
  output S_1,
  output S_2,
  output S_3,
  output S_4,
  output S_5,
  output S_6,
  output S_7
);

  wire multiplexer_1_out, multiplexer_2_out, multiplexer_3_out, multiplexer_4_out, multiplexer_5_out,
       multiplexer_6_out, multiplexer_7_out, multiplexer_8_out;

  Multiplexer multiplexer_1 (.sel(D_0), .in_0(E_7), .in_1(E_6), .out(multiplexer_1_out));
  Multiplexer multiplexer_2 (.sel(D_0), .in_0(E_6), .in_1(E_5), .out(multiplexer_2_out));
  Multiplexer multiplexer_3 (.sel(D_0), .in_0(E_5), .in_1(E_4), .out(multiplexer_3_out));
  Multiplexer multiplexer_4 (.sel(D_0), .in_0(E_4), .in_1(E_3), .out(multiplexer_4_out));
  Multiplexer multiplexer_5 (.sel(D_0), .in_0(E_3), .in_1(E_2), .out(multiplexer_5_out));
  Multiplexer multiplexer_6 (.sel(D_0), .in_0(E_2), .in_1(E_1), .out(multiplexer_6_out));
  Multiplexer multiplexer_7 (.sel(D_0), .in_0(E_1), .in_1(E_0), .out(multiplexer_7_out));
  Multiplexer multiplexer_8 (.sel(D_0), .in_0(E_0), .in_1(1'b0), .out(multiplexer_8_out));
  Multiplexer multiplexer_9 (.sel(D_1), .in_0(multiplexer_1_out), .in_1(multiplexer_3_out), .out(S_7));
  Multiplexer multiplexer_10 (.sel(D_1), .in_0(multiplexer_2_out), .in_1(multiplexer_4_out), .out(S_6));
  Multiplexer multiplexer_11 (.sel(D_1), .in_0(multiplexer_3_out), .in_1(multiplexer_5_out), .out(S_5));
  Multiplexer multiplexer_12 (.sel(D_1), .in_0(multiplexer_4_out), .in_1(multiplexer_6_out), .out(S_4));
  Multiplexer multiplexer_13 (.sel(D_1), .in_0(multiplexer_5_out), .in_1(multiplexer_7_out), .out(S_3));
  Multiplexer multiplexer_14 (.sel(D_1), .in_0(multiplexer_6_out), .in_1(multiplexer_8_out), .out(S_2));
  Multiplexer multiplexer_15 (.sel(D_1), .in_0(multiplexer_7_out), .in_1(1'b0), .out(S_1));
  Multiplexer multiplexer_16 (.sel(D_1), .in_0(multiplexer_8_out), .in_1(1'b0), .out(S_0));
endmodule
