// Digital circuit CC_8bits-1.dig as structural Verilog
module CC_8bits_1 (
  input  P_0,
  input  P_1,
  input  P_2,
  input  P_3,
  input  P_4,
  input  P_5,
  input  G_0,
  input  G_1,
  input  G_2,
  input  G_3,
  input  G_4,
  input  G_5,
  input  G_6,
  input  P_6,
  input  C_0,
  input  G_7,
  input  P_7,
  output S_0,
  output S_1,
  output S_2,
  output S_3,
  output S_4,
  output S_5,
  output S_6,
  output S_7,
  output S_8
);

  wire and_1_out, and_2_out, and_3_out, and_4_out, and_5_out, and_6_out, and_7_out, and_8_out;

  and and_1 (and_1_out, P_0, C_0);
  or or_1 (S_1, G_0, and_1_out);
  and and_2 (and_2_out, P_1, S_1);
  or or_2 (S_2, G_1, and_2_out);
  and and_3 (and_3_out, P_2, S_2);
  or or_3 (S_3, G_2, and_3_out);
  and and_4 (and_4_out, P_3, S_3);
  or or_4 (S_4, G_3, and_4_out);
  and and_5 (and_5_out, G_4, S_4);
  or or_5 (S_5, P_4, and_5_out);
  and and_6 (and_6_out, P_5, S_5);
  or or_6 (S_6, G_5, and_6_out);
  and and_7 (and_7_out, P_6, S_6);
  or or_7 (S_7, G_6, and_7_out);
  and and_8 (and_8_out, P_7, S_7);
  or or_8 (S_8, G_7, and_8_out);

  assign S_0 = C_0;
endmodule
