// Digital circuit Multiplexeru_2_entrees.dig as structural Verilog
module Multiplexeru_2_entrees (
  input  X,
  input  Y,
  input  Z,
  output S0
);

  wire and_1_out, and_2_out, not_1_out;

  not not_1 (not_1_out, Z);
  and and_1 (and_1_out, X, not_1_out);
  and and_2 (and_2_out, Y, Z);
  or or_1 (S0, and_1_out, and_2_out);
endmodule
