// Digital circuit Multiplexeur_8_entrees_non-recursif.dig as structural Verilog
module Multiplexeur_8_entrees_non_recursif (
  input  E0,
  input  E1,
  input  E2,
  input  E3,
  input  E4,
  input  E5,
  input  E6,
  input  E7,
  input  E8,
  input  E9,
  input  E10,
  output S0
);

  wire and_1_out, and_2_out, and_3_out, and_4_out, and_5_out, and_6_out, and_7_out, and_8_out, and_9_out,
       and_10_out, and_11_out, and_12_out, and_13_out, and_14_out, and_15_out, and_16_out, and_17_out,
       and_18_out, and_19_out, and_20_out, and_21_out, and_22_out, and_23_out, and_24_out, not_1_out,
       not_2_out, not_3_out, or_1_out, or_2_out, or_3_out, or_4_out, or_5_out, or_6_out;

  not not_1 (not_1_out, E8);
  not not_2 (not_2_out, E9);
  not not_3 (not_3_out, E10);
  and and_1 (and_1_out, not_1_out, not_2_out);
  and and_2 (and_2_out, E8, not_2_out);
  and and_3 (and_3_out, E9, not_1_out);
  and and_4 (and_4_out, E8, E9);
  and and_5 (and_5_out, not_1_out, not_2_out);
  and and_6 (and_6_out, E8, not_2_out);
  and and_7 (and_7_out, not_1_out, E9);
  and and_8 (and_8_out, E8, E9);
  and and_9 (and_9_out, and_2_out, not_3_out);
  and and_10 (and_10_out, and_3_out, not_3_out);
  and and_11 (and_11_out, and_4_out, not_3_out);
  and and_12 (and_12_out, and_5_out, E10);
  and and_13 (and_13_out, and_6_out, E10);
  and and_14 (and_14_out, and_7_out, E10);
  and and_15 (and_15_out, and_8_out, E10);
  and and_16 (and_16_out, and_1_out, not_3_out);
  and and_17 (and_17_out, E0, and_16_out);
  and and_18 (and_18_out, E1, and_9_out);
  and and_19 (and_19_out, E2, and_10_out);
  and and_20 (and_20_out, E3, and_11_out);
  and and_21 (and_21_out, E4, and_12_out);
  and and_22 (and_22_out, E5, and_13_out);
  and and_23 (and_23_out, E6, and_14_out);
  and and_24 (and_24_out, E7, and_15_out);
  or or_1 (or_1_out, and_17_out, and_18_out);
  or or_2 (or_2_out, and_19_out, and_20_out);
  or or_3 (or_3_out, and_21_out, and_22_out);
  or or_4 (or_4_out, and_23_out, and_24_out);
  or or_5 (or_5_out, or_1_out, or_2_out);
  or or_6 (or_6_out, or_3_out, or_4_out);
  or or_7 (S0, or_5_out, or_6_out);
endmodule
