// Digital circuit multiplexeur_8_entrees.dig as structural Verilog
module multiplexeur_8_entrees (
  input  E0,
  input  E1,
  input  E2,
  input  E3,
  input  E4,
  input  E5,
  input  E6,
  input  E7,
  input  Z0,
  input  Z1,
  input  Z2,
  output S0
);

  wire multiplexeru_2_entrees_1_s0, multiplexeru_2_entrees_2_s0, multiplexeru_2_entrees_3_s0,
       multiplexeru_2_entrees_5_s0, multiplexeru_2_entrees_6_s0;

  Multiplexeru_2_entrees multiplexeru_2_entrees_1 (.X(E0), .Y(E1), .Z(Z0), .S0(multiplexeru_2_entrees_1_s0));
  Multiplexeru_2_entrees multiplexeru_2_entrees_2 (.X(E2), .Y(E3), .Z(Z0), .S0(multiplexeru_2_entrees_2_s0));
  Multiplexeru_2_entrees multiplexeru_2_entrees_3 (.X(E4), .Y(E5), .Z(Z0), .S0(multiplexeru_2_entrees_3_s0));
  Multiplexeru_2_entrees multiplexeru_2_entrees_4 (.X(E6), .Y(E7), .Z(Z0), .S0(multiplexeru_2_entrees_3_s0));
  Multiplexeru_2_entrees multiplexeru_2_entrees_5 (
    .X(multiplexeru_2_entrees_1_s0), .Y(multiplexeru_2_entrees_2_s0), .Z(Z1), .S0(multiplexeru_2_entrees_5_s0));
  Multiplexeru_2_entrees multiplexeru_2_entrees_6 (
    .X(multiplexeru_2_entrees_3_s0), .Y(multiplexeru_2_entrees_3_s0), .Z(Z1), .S0(multiplexeru_2_entrees_6_s0));
  Multiplexeru_2_entrees multiplexeru_2_entrees_7 (
    .X(multiplexeru_2_entrees_5_s0), .Y(multiplexeru_2_entrees_6_s0), .Z(Z2), .S0(S0));
endmodule
