// Digital circuit ADD 1bit.dig as structural Verilog
module ADD_1bit (
  input  A,
  input  B,
  input  Cin,
  output Cout,
  output S
);

  wire and_1_out, and_2_out, and_3_out, or_1_out, xor_1_out;

  xor xor_1 (xor_1_out, Cin, B);
  and and_1 (and_1_out, B, A);
  and and_2 (and_2_out, B, Cin);
  xor xor_2 (S, xor_1_out, A);
  and and_3 (and_3_out, Cin, A);
  or or_1 (or_1_out, and_2_out, and_1_out);
  or or_2 (Cout, and_3_out, or_1_out);
endmodule
