// Digital circuit ADD 8 Bit.dig as structural Verilog
module ADD_8_Bit (
  input  A0,
  input  A1,
  input  A2,
  input  A3,
  input  B0,
  input  B1,
  input  B2,
  input  B3,
  input  Cin,
  input  A4,
  input  B4,
  input  A5,
  input  B5,
  input  A6,
  input  B6,
  input  A7,
  input  B7,
  output S0,
  output S1,
  output S2,
  output S3,
  output S4,
  output S5,
  output S6,
  output S7,
  output Cout
);

  wire add_1bit_2_cout, add_1bit_3_cout, add_1bit_4_cout, add_1bit_5_cout, add_1bit_6_cout, add_1bit_7_cout,
       add_1bit_8_cout;

  ADD_1bit add_1bit_1 (.A(A7), .B(B7), .Cin(add_1bit_2_cout), .Cout(Cout), .S(S7));
  ADD_1bit add_1bit_2 (.A(A6), .B(B6), .Cin(add_1bit_3_cout), .Cout(add_1bit_2_cout), .S(S6));
  ADD_1bit add_1bit_3 (.A(A5), .B(B5), .Cin(add_1bit_4_cout), .Cout(add_1bit_3_cout), .S(S5));
  ADD_1bit add_1bit_4 (.A(A4), .B(B4), .Cin(add_1bit_5_cout), .Cout(add_1bit_4_cout), .S(S4));
  ADD_1bit add_1bit_5 (.A(A3), .B(B3), .Cin(add_1bit_6_cout), .Cout(add_1bit_5_cout), .S(S3));
  ADD_1bit add_1bit_6 (.A(A2), .B(B2), .Cin(add_1bit_7_cout), .Cout(add_1bit_6_cout), .S(S2));
  ADD_1bit add_1bit_7 (.A(A1), .B(B1), .Cin(add_1bit_8_cout), .Cout(add_1bit_7_cout), .S(S1));
  ADD_1bit add_1bit_8 (.A(A0), .B(B0), .Cin(Cin), .Cout(add_1bit_8_cout), .S(S0));
endmodule
