// Digital circuit ADDPG 1bit.dig as structural Verilog
module ADDPG_1bit (
  input  Ai,
  input  Bi,
  input  Cin,
  output Si,
  output Gi,
  output Pi
);

  wire xor_1_out;

  xor xor_1 (xor_1_out, Ai, Bi);
  or or_1 (Pi, Ai, Bi);
  and and_1 (Gi, Ai, Bi);
  xor xor_2 (Si, xor_1_out, Cin);
endmodule
