// Digital circuit CC 4 bits.dig as structural Verilog
module CC_4_bits (
  input  G0,
  input  G1,
  input  G2,
  input  G3,
  input  P0,
  input  P1,
  input  P2,
  input  P3,
  input  Cin,
  output C0,
  output C1,
  output C2,
  output C3
);

  wire and_1_out, and_2_out, and_3_out, and_4_out;

  and and_1 (and_1_out, C2, P3);
  and and_2 (and_2_out, Cin, P0);
  and and_3 (and_3_out, C0, P1);
  and and_4 (and_4_out, C1, P2);
  or or_1 (C0, and_2_out, G0);
  or or_2 (C1, and_3_out, G1);
  or or_3 (C2, and_4_out, G2);
  or or_4 (C3, and_1_out, G3);
endmodule
