// Digital circuit Decodeur 2 vers 4.dig as structural Verilog
module Decodeur_2_vers_4 (
  input  E0,
  input  E1,
  output S0,
  output S1,
  output S2,
  output S3
);

  and and_1 (S0, ~E0, ~E1);  // And
  and and_2 (S1, ~E0, E1);  // And
  and and_3 (S2, E0, ~E1);  // And
  and and_4 (S3, E0, E1);
endmodule
