// Digital circuit Decodeur 3 vers 8.dig as structural Verilog
module Decodeur_3_vers_8 (
  input  E0,
  input  E1,
  input  E2,
  output S0,
  output S1,
  output S2,
  output S3,
  output S4,
  output S5,
  output S6,
  output S7
);

  wire and_1_out, and_2_out, and_3_out, and_4_out, and_5_out, and_6_out, and_7_out, and_8_out;

  and and_1 (and_1_out, ~E0, ~E1);  // And
  and and_2 (and_2_out, ~E0, ~E1);  // And
  and and_3 (and_3_out, ~E0, E1);  // And
  and and_4 (and_4_out, ~E0, E1);  // And
  and and_5 (and_5_out, E0, ~E1);  // And
  and and_6 (and_6_out, E0, ~E1);  // And
  and and_7 (and_7_out, E0, E1);
  and and_8 (and_8_out, E0, E1);
  and and_9 (S0, and_1_out, ~E2);  // And
  and and_10 (S1, and_2_out, E2);
  and and_11 (S2, and_3_out, ~E2);  // And
  and and_12 (S3, and_4_out, E2);
  and and_13 (S4, and_5_out, ~E2);  // And
  and and_14 (S5, and_6_out, E2);
  and and_15 (S6, and_7_out, ~E2);  // And
  and and_16 (S7, and_8_out, E2);
endmodule
