// Digital circuit Mux 2-1.dig as structural Verilog
module Mux_2_1 (
  input  E0,
  input  E1,
  input  INT,
  output S
);

  wire and_1_out, and_2_out;

  and and_1 (and_1_out, E0, ~INT);  // And
  and and_2 (and_2_out, E1, INT);
  or or_1 (S, and_1_out, and_2_out);
endmodule
