// Digital circuit Mux 8 non recursif.dig as structural Verilog
module Mux_8_non_recursif (
  input  E0,
  input  E1,
  input  E2,
  input  E3,
  input  E4,
  input  E5,
  input  E6,
  input  E7,
  input  C0,
  input  C1,
  input  C2,
  output out_12
);

  wire and_1_out, and_2_out, and_3_out, and_4_out, and_5_out, and_6_out, and_7_out, and_8_out, and_9_out,
       and_10_out, and_11_out, and_12_out, and_13_out, and_14_out, or_1_out, or_2_out, or_3_out, or_4_out,
       or_5_out, or_6_out;

  and and_1 (and_1_out, E0, ~C0);  // And
  and and_2 (and_2_out, E1, C0);
  and and_3 (and_3_out, E2, ~C0);  // And
  and and_4 (and_4_out, E3, C0);
  and and_5 (and_5_out, E4, ~C0);  // And
  and and_6 (and_6_out, E5, C0);
  and and_7 (and_7_out, E6, ~C0);  // And
  and and_8 (and_8_out, E7, C0);
  or or_1 (or_1_out, and_1_out, and_2_out);
  or or_2 (or_2_out, and_3_out, and_4_out);
  or or_3 (or_3_out, and_5_out, and_6_out);
  or or_4 (or_4_out, and_7_out, and_8_out);
  and and_9 (and_9_out, or_1_out, ~C1);  // And
  and and_10 (and_10_out, or_2_out, C1);
  and and_11 (and_11_out, or_3_out, ~C1);  // And
  and and_12 (and_12_out, or_4_out, C1);
  or or_5 (or_5_out, and_9_out, and_10_out);
  or or_6 (or_6_out, and_11_out, and_12_out);
  and and_13 (and_13_out, or_5_out, ~C2);  // And
  and and_14 (and_14_out, or_6_out, C2);
  or or_7 (out_12, and_13_out, and_14_out);
endmodule
