// Digital circuit Mux 8-1 recursif.dig as structural Verilog
module Mux_8_1_recursif (
  input  E0,
  input  E1,
  input  E2,
  input  E3,
  input  E4,
  input  E5,
  input  E6,
  input  E7,
  input  C0,
  input  C1,
  input  C2,
  output out_9
);

  wire mux_2_1_1_s, mux_2_1_2_s, mux_2_1_3_s, mux_2_1_4_s, mux_2_1_5_s, mux_2_1_6_s;

  Mux_2_1 mux_2_1_1 (.E0(E0), .E1(E1), .INT(C0), .S(mux_2_1_1_s));
  Mux_2_1 mux_2_1_2 (.E0(E2), .E1(E3), .INT(C0), .S(mux_2_1_2_s));
  Mux_2_1 mux_2_1_3 (.E0(E4), .E1(E5), .INT(C0), .S(mux_2_1_3_s));
  Mux_2_1 mux_2_1_4 (.E0(E6), .E1(E7), .INT(C0), .S(mux_2_1_4_s));
  Mux_2_1 mux_2_1_5 (.E0(mux_2_1_1_s), .E1(mux_2_1_2_s), .INT(C1), .S(mux_2_1_5_s));
  Mux_2_1 mux_2_1_6 (.E0(mux_2_1_3_s), .E1(mux_2_1_4_s), .INT(C1), .S(mux_2_1_6_s));
  Mux_2_1 mux_2_1_7 (.E0(mux_2_1_5_s), .E1(mux_2_1_6_s), .INT(C2), .S(out_9));
endmodule
